# Fritzing sketch Mood-lamp (saved by Fritzing 0.9.4)
circuit board: 7.13872cm x 6.73804cm
breadboards: 1

parts:
  NeoPixel_Extra_Header = Dagu DGServo 9g header (male) [package=THT]
  part = 24 NeoPixel Ring [part_number=1586]
  BMP280_Breakout1 = BMP280 Breakout Board [part_number=BMP280]
  I2C_extra_Header = Header 4 [package=molex-1x4_lock]
  WeMos_D1_Mini2 = WeMos D1 Mini
  NeoPixelHeader = Header 4 [package=molex-1x4_lock]
  Main_Switch = SPST Switch [package=switch-spdt]
  Power = Header 2 [package=screwterminal-3.5mm-2_lock]

nets:
  GND: NeoPixel_Extra_Header.gnd, part.GND, BMP280_Breakout1.GND, I2C_extra_Header.2, WeMos_D1_Mini2.G, NeoPixelHeader.1, Power.2
  VCC: NeoPixel_Extra_Header.Vcc, part.VDD, BMP280_Breakout1.VCC, I2C_extra_Header.1, WeMos_D1_Mini2.5V, NeoPixelHeader.2, Main_Switch.O
  N1: NeoPixel_Extra_Header.pulse, part.OUT, NeoPixelHeader.4
  N2: part.IN, WeMos_D1_Mini2.D2, NeoPixelHeader.3
  N3: BMP280_Breakout1.SCL, I2C_extra_Header.3, WeMos_D1_Mini2.D3
  N4: BMP280_Breakout1.SDA, I2C_extra_Header.4, WeMos_D1_Mini2.D4
  N5: Main_Switch.P, Power.1

notes:
  Extra RGB
  Extra I2C

custom parts:
  24 NeoPixel Ring: 24 ultra bright smart LED NeoPixels are arranged in a circle with 2.6" (66mm) outer diameter. The rings are 'chainable' - connect the output pin of one to the input pin of another. Use only one microcontroller pin to control as many as you can chain together! Each LED is addressable as the driver chip is inside the LED. Each one has ~18mA constant current drive so the color will be very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
  BMP280 Breakout Board: This is a breakout board for the Bosch Sensortec BMP280, "an absolute barometric pressure sensor especially designed for mobile applications." The operation range is 300 to 1100 hPa. Supply voltage is 1.2 to 3.6V. Operating temperature range is -40 to +85 °C.
