# Fritzing sketch PCB-LCD_BME280 (saved by Fritzing 0.9.4)
circuit board: 8.57117cm x 7.22238cm
breadboards: 1

parts:
  LCD_I2C = LCD1602-I2C
  NodeMCU = NodeMCU V1.0
  BMP280_Breakout1 = BMP280 Breakout Board [part_number=BMP280]
  R1 = Resistor [tolerance=±5% resistance=220 package=THT]
  LED1 = LED - 5mm [color="Red (633nm)" package="5 mm [THT]"]
  alimentación_5v = female pin header, 2 pins [form="♀ (female)"]
  Componente1 = TP4056 Charger  # not connected
  J1_-_battery = Generic female header - 2 pins [form="♀ (female)" package=THT]  # not connected
  R2 = Photocell (LDR) [package=THT]  # not connected
  JP1 = Header 2 [package=screwterminal-3.5mm-2_lock]  # not connected

nets:
  GND: LCD_I2C.GND, NodeMCU.GND, BMP280_Breakout1.GND, LED1.cathode, alimentación_5v.pin2
  VCC: LCD_I2C.VCC, NodeMCU.Vin, BMP280_Breakout1.VCC, R1.Pin_0, alimentación_5v.pin1
  N1: LCD_I2C.SDA, NodeMCU.D2, BMP280_Breakout1.SDA
  N2: LCD_I2C.SCL, NodeMCU.D1, BMP280_Breakout1.SCL
  N3: R1.Pin_1, LED1.anode

notes:
  5V
  I2C
  SCL y SDA
  I2C
  D1 - SCL
  D2 - SDA
  LDR, conector solar y

custom parts:
  LCD1602-I2C: A standard character display, usually with 2x16 characters. Comes in many colors with LCM1602 IIC attached.
  NodeMCU V1.0: ESP8266 based NodeMCU
  BMP280 Breakout Board: This is a breakout board for the Bosch Sensortec BMP280, "an absolute barometric pressure sensor especially designed for mobile applications." The operation range is 300 to 1100 hPa. Supply voltage is 1.2 to 3.6V. Operating temperature range is -40 to +85 °C.
  Generic female header - 2 pins: Generic female header
